# Fritzing sketch ChemE Car Electrical Team 2019 (saved by Fritzing 0.9.3b)
circuit board: 8.46667cm x 5.64444cm
perfboards: 1

parts:
  Part1 = Arduino Nano (Rev3.0) (ICSP)  # not connected
  J1_-_Nano_Connection = female pin header, 15 pins [form="♀ (female)"]  # not connected
  J2_-_Nano_Connection = female pin header, 15 pins [form="♀ (female)"]  # not connected
  J1 = female pin header, 6 pins [form="♀ (female)"]  # not connected
  J2 = female pin header, 6 pins [form="♀ (female)"]  # not connected
  J3 = female pin header, 6 pins [form="♀ (female)"]  # not connected
  R1 = Resistor [tolerance=±5% resistance=100k package=THT]
  R2 = Resistor [tolerance=±5% resistance=100k package=THT]  # not connected
  R3 = Resistor [tolerance=±5% resistance=100k package=THT]  # not connected
  R4 = Resistor [tolerance=±5% resistance=100k package=THT]

nets:
  N1: R1.Pin_1, R4.Pin_1

notes:
  white wires: connections on back of PCB
